# Fritzing sketch master (saved by Fritzing 0.9.3b)

parts:
  WeMos_D1_Mini1 = WeMos D1 Mini
  TP4056 = TP4056 Module
  BAT1 = Battery Holders [package=battery-aa]
  Switch = Toggle Switch [package=THT]
  Microphone_module = Adafruit MAX4466 Electret Microphone Amplifier
  Rotary_Encoder = KY-040 Rotary encoder [package=THT]
  LED1 = LED - 5mm [color="Red (633nm)" package="5 mm [THT]"]
  R1 = Resistor [tolerance=±5% resistance=330 package=THT]

nets:
  3V3: WeMos_D1_Mini1.3V3, Microphone_module.VCC
  N1: WeMos_D1_Mini1.5V, TP4056.pin5
  N2: WeMos_D1_Mini1.A0, Microphone_module.OUT
  N3: WeMos_D1_Mini1.D1, LED1.cathode
  N4: WeMos_D1_Mini1.D5, Rotary_Encoder.SW
  N5: WeMos_D1_Mini1.D6, Rotary_Encoder.CLK
  N6: WeMos_D1_Mini1.D7, Rotary_Encoder.DT
  N7: WeMos_D1_Mini1.G, Switch.COM, Microphone_module.GND, R1.Pin_1
  N8: TP4056.pin2, Switch.L1
  N9: TP4056.pin3, BAT1.-
  N10: TP4056.pin4, BAT1.+

custom parts:
  WeMos D1 Mini: The D1 mini is a mini wifi board based on ESP-8266EX.
  TP4056 Module: TP4056 Lithium Battery Charge Management Module Links: TP4056 website
  Battery Holders: Battery Holders Various common sizes : AA, AAA, 20mm coin cell and 12mm coin cell.
  Adafruit MAX4466 Electret Microphone Amplifier: Add an ear to your project with this well-designed electret microphone amplifier. This fully assembled and tested board comes with a 20-20KHz electret microphone soldered on. For the amplification, we use the Maxim MAX4466, an op-amp specifically designed for this delicate task! The amplifier has excellent power supply noise rejection, so this amplifier sounds really good and isn't nearly as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
  KY-040 Rotary encoder: KY-040 Rotary Encoder with switch on breakout borad from AZ Delivery
