# Fritzing sketch slave (saved by Fritzing 0.9.3b)

parts:
  Espessif_Serial_Wifi_Module = ESP8266 ESP01 [part_number="ESP8266 - ESP-01s" package=THT]
  220VAC_-_5VDC = generic-ac-power-supply [package=THT]
  5V_DC_to_3_3V_DC_voltage_regulator = Voltage Regulator -- 3.3 V -- LM1117
  WS2812_neopixels = WS2812 RGB LED strip

nets:
  GND: Espessif_Serial_Wifi_Module.GND, 220VAC_-_5VDC.pin3#3, WS2812_neopixels.GND
  N1: Espessif_Serial_Wifi_Module.GPIO02, WS2812_neopixels.DIN
  N2: Espessif_Serial_Wifi_Module.CH_PD, 5V_DC_to_3_3V_DC_voltage_regulator.OUT
  N3: 220VAC_-_5VDC.pin3#2, 5V_DC_to_3_3V_DC_voltage_regulator.IN, WS2812_neopixels.VCC

notes:
  to 220V AC...

custom parts:
  ESP8266 ESP01: Generic WiFi Module based on the ESP8266 with onboard PCB antenna and UART communications
  generic-ac-power-supply: Generic ac power supply module. Use as is, or customize the svgs to fit your particular device (as they are all different.) Provides AC input and single DC output. PCB is generic and will need modifications if you intend to do a pcb mount.
  Voltage Regulator -- 3.3 V -- LM1117: LM1117-3.3 Voltage regulator, 3.3 V output. Note that the pinout order is not the same as LM7805 or LM7833.
  WS2812 RGB LED strip: WS2812 strip
